// Logisim project CPU Backup 7.circ as structural Verilog: 8 circuits, main circuit main
module main (
  output MAR_En,
  output Memory_En,
  output Memory_Wr,
  output MBR_En
);

  wire clock_1_out;
  wire [11:0] MAR_q;
  wire [15:0] MBR_q, ram_1_data;

  Clock clock_1 (.out(clock_1_out));
  Register #(.width(12), .trigger("falling")) MAR (.D(12'h1), .en(MAR_En), .Q(MAR_q), .clk(clock_1_out));  // open: clr
  Register #(.width(16), .trigger("falling")) MBR (
    .D(ram_1_data), .en(MBR_En), .Q(MBR_q), .clk(clock_1_out));  // open: clr
  RAM #(.addrWidth(12), .dataWidth(16)) ram_1 (
    .addr(MAR_q), .data(ram_1_data), .sel(Memory_En), .clk(clock_1_out), .ld(Memory_Wr));  // open: clr
  Hex_Digit_Display hex_digit_display_1 (.value(ram_1_data[11:8]));  // open: dp
  Hex_Digit_Display hex_digit_display_2 (.value(ram_1_data[15:12]));  // open: dp
  Hex_Digit_Display hex_digit_display_3 (.value(MBR_q[11:8]));  // open: dp
  Hex_Digit_Display hex_digit_display_4 (.value(MBR_q[15:12]));  // open: dp
  Hex_Digit_Display hex_digit_display_5 (.value(ram_1_data[7:4]));  // open: dp
  Hex_Digit_Display hex_digit_display_6 (.value(ram_1_data[3:0]));  // open: dp
  Hex_Digit_Display hex_digit_display_7 (.value(MBR_q[7:4]));  // open: dp
  Hex_Digit_Display hex_digit_display_8 (.value(MBR_q[3:0]));  // open: dp
endmodule

module Draft_CPU (
  input  in_1
);

  wire _0_out, _1_out, _2_out, _3_out, _4_out, _5_out, _6_out, _7_out, _8_out, _9_out, A0_out, A1_2_out,
       A1_out, A2_out, A3_out, A_out, and_1_out, and_2_out, and_3_out, and_4_out, and_5_out, and_6_out,
       and_7_out, and_8_out, and_9_out, and_10_out, and_11_out, and_12_out, and_13_out, and_14_out, B_out,
       C_out, Clear_out, clock_1_out, controlled_inverter_1_out, CR_out, D_out, E_out, Enter_out, F_out,
       IN_out, IncrPC_out, InRegA_2_q, InRegA_3_q, JMP_out, L1_out, L2_out, L3_out, LAlt_out, MR_out, MW_out,
       not_1_out, or_1_out, or_2_out, or_3_out, or_4_out, or_5_out, or_6_out, or_7_out, or_8_out, or_9_out,
       or_10_out, OUT_out, P0_out, P1_out, P2_out, P3_out, P4_out, P5_out, priority_encoder_1_gs,
       Rung_Counter_t0, Rung_Counter_t1, Rung_Counter_t2, Rung_Counter_t3, Rung_Counter_t4, Rung_Counter_t5,
       S1_out, S2_out, S3_out, selector_1__1__load_x, selector_1__2__store_x, selector_1__3__add_x,
       selector_1__4__subt_x, selector_1__5__input, selector_1__6__output, selector_1__7__halt,
       selector_1__8__skipcond__c, selector_1__9__jump_x, selector_1_error, SKIP_out,
       SkipCond_Check_skipconfirmed, SU1_out, SU2_out, SU3_out, T0_out, T1_out, T2_out, T3_out, T4_out,
       T5_out, TempClockStop_q, xor_1_out;
  wire [3:0] InRegC_q, OutReg_q_2, OutReg_q_3;
  wire [7:0] OutReg_q;
  wire [11:0] InRegMaster_q, MAR_q, PC_q, priority_encoder_1_out;
  wire [15:0] AC_q, ALU_output, bit_extender_1_out, bit_extender_2_out, bit_extender_3_out,
       controlled_buffer_1_out, IR_q, MBR_q, multiplexer_1_out, multiplexer_2_out, multiplexer_3_out,
       ram_1_data;

  Button _0 (.out(_0_out));
  Button _4 (.out(_4_out));
  Button _8 (.out(_8_out));
  Button C (.out(C_out));
  Button _1 (.out(_1_out));
  Button _5 (.out(_5_out));
  Button _9 (.out(_9_out));
  Button D (.out(D_out));
  Button _2 (.out(_2_out));
  Button _6 (.out(_6_out));
  Button A (.out(A_out));
  Button E (.out(E_out));
  Button _3 (.out(_3_out));
  Button _7 (.out(_7_out));
  Button B (.out(B_out));
  Button F (.out(F_out));
  Button Clear (.out(Clear_out));
  Button Enter (.out(Enter_out));
  Hex_Digit_Display hex_digit_display_1 (.value(InRegC_q));  // open: dp
  Priority_Encoder #(.select(4), .disabled(0)) priority_encoder_1 (
    .in0(_0_out), .in1(_1_out), .in2(_2_out), .in3(_3_out), .in4(_4_out), .in5(_5_out), .in6(_6_out),
    .in7(_7_out), .in8(_8_out), .in9(_9_out), .in10(A_out), .in11(B_out), .in12(C_out), .in13(D_out),
    .in14(E_out), .in15(F_out), .out(priority_encoder_1_out[3:0]), .gs(priority_encoder_1_gs));  // open: en_out, en_in
  Hex_Digit_Display hex_digit_display_2 (.value(priority_encoder_1_out[11:8]));  // open: dp
  Hex_Digit_Display hex_digit_display_3 (.value(priority_encoder_1_out[7:4]));  // open: dp
  Register #(.width(4)) InRegA (
    .D(priority_encoder_1_out[3:0]), .Q(priority_encoder_1_out[7:4]), .clk(priority_encoder_1_gs),
    .clr(or_1_out));  // open: en
  or or_1 (or_1_out, Clear_out, Enter_out);
  Register #(.width(4)) InRegB (
    .D(priority_encoder_1_out[7:4]), .Q(priority_encoder_1_out[11:8]), .clk(priority_encoder_1_gs),
    .clr(or_2_out));  // open: en
  or or_2 (or_2_out, Clear_out, Enter_out);
  Register #(.width(4)) InRegC (
    .D(priority_encoder_1_out[11:8]), .Q(InRegC_q), .clk(priority_encoder_1_gs), .clr(or_3_out));  // open: en
  or or_3 (or_3_out, Clear_out, Enter_out);
  assign controlled_inverter_1_out = Clear_out ? ~or_3_out : 1'bz;  // Controlled_Inverter controlled_inverter_1
  or or_4 (or_4_out, priority_encoder_1_gs, Enter_out);
  Register #(.width(1)) InRegA_2 (.D(Enter_out), .Q(InRegA_2_q), .clk(Enter_out), .clr(and_12_out));  // open: en
  Hex_Digit_Display hex_digit_display_4 (.value(controlled_buffer_1_out[11:8]));  // open: dp
  Hex_Digit_Display hex_digit_display_5 (.value(controlled_buffer_1_out[15:12]));  // open: dp
  Register #(.width(1)) InRegA_3 (.D(Enter_out), .Q(InRegA_3_q), .clk(Enter_out), .clr(and_12_out));  // open: en
  Register #(.width(1)) TempClockStop (
    .D(selector_1__5__input), .Q(TempClockStop_q), .clk(selector_1__5__input), .clr(and_12_out));  // open: en
  Hex_Digit_Display hex_digit_display_6 (.value(controlled_buffer_1_out[7:4]));  // open: dp
  Hex_Digit_Display hex_digit_display_7 (.value(controlled_buffer_1_out[3:0]));  // open: dp
  and and_1 (and_1_out, ~P5_out, ~P4_out, P3_out);  // AND_Gate
  and and_2 (and_2_out, ~P5_out, P4_out, ~P3_out);  // AND_Gate
  and and_3 (and_3_out, ~P5_out, P4_out, P3_out);  // AND_Gate
  Multiplexer #(.width(16), .enable("false")) multiplexer_1 (
    .in0(controlled_buffer_1_out), .in1(MBR_q), .out(multiplexer_1_out), .sel(LAlt_out));
  and and_4 (and_4_out, P5_out, ~P4_out, ~P3_out);  // AND_Gate
  and and_5 (and_5_out, P5_out, P4_out, ~P3_out);  // AND_Gate
  and and_6 (and_6_out, P5_out, P4_out, P3_out);
  not not_1 (not_1_out, and_2_out);
  or or_5 (or_5_out, and_2_out, IncrPC_out);
  Multiplexer #(.width(16), .enable("false")) multiplexer_2 (
    .in0(controlled_buffer_1_out), .in1(AC_q), .out(multiplexer_2_out), .sel(LAlt_out));
  Multiplexer #(.width(16), .enable("false")) multiplexer_3 (
    .in0(multiplexer_1_out), .in1(ALU_output), .out(multiplexer_3_out), .sel(or_7_out));
  xor xor_1 (xor_1_out, InRegA_3_q, TempClockStop_q);
  LED ERROR__no_opcode_16_found (.in(selector_1_error));
  RAM #(.addrWidth(12), .dataWidth(16), .bus("separate")) ram_1 (
    .addr(MAR_q), .din(controlled_buffer_1_out), .data(ram_1_data), .clk(MW_out));  // open: str, sel, ld, clr
  Register #(.width(12), .trigger("high")) MAR (
    .D(controlled_buffer_1_out[11:0]), .Q(MAR_q), .clk(and_1_out));  // open: en, clr
  Counter #(.width(12), .max('hfff), .ongoal("stay")) PC (
    .load(and_2_out), .D(controlled_buffer_1_out[11:0]), .count(not_1_out), .Q(PC_q), .clk(or_5_out));  // open: carry, clr
  Register #(.width(16), .trigger("high")) MBR (.D(multiplexer_2_out), .Q(MBR_q), .clk(and_3_out));  // open: en, clr
  ALU ALU (.MBR(MBR_q), .AC(AC_q), .A1(A1_2_out), .A0(A0_out), .Output(ALU_output));
  Register #(.width(16), .trigger("falling")) AC (.D(multiplexer_3_out), .Q(AC_q), .clk(and_4_out));  // open: en, clr
  Register #(.width(16), .trigger("high")) OutReg (
    .D(controlled_buffer_1_out), .Q({OutReg_q_3, OutReg_q_2, OutReg_q}), .clk(and_5_out));  // open: en, clr
  assign bit_extender_1_out = {{4{1'b0}}, InRegMaster_q};  // Bit_Extender bit_extender_1
  Register #(.width(12)) InRegMaster (
    .D(priority_encoder_1_out), .Q(InRegMaster_q), .clk(or_4_out), .clr(or_6_out));  // open: en
  or or_6 (or_6_out, controlled_inverter_1_out, and_12_out);
  and and_7 (and_7_out, InRegA_2_q, and_12_out);
  Register #(.width(16), .trigger("high")) IR (
    .D(controlled_buffer_1_out), .Q(IR_q), .clk(and_6_out));  // open: en, clr
  assign controlled_buffer_1_out = MR_out ? ram_1_data : 16'bz;  // Controlled_Buffer controlled_buffer_1
  assign bit_extender_2_out = {{4{1'b0}}, MAR_q};  // Bit_Extender bit_extender_2
  assign controlled_buffer_1_out = and_8_out ? bit_extender_2_out : 16'bz;  // Controlled_Buffer controlled_buffer_2
  and and_8 (and_8_out, ~P2_out, ~P1_out, P0_out);  // AND_Gate
  assign controlled_buffer_1_out = and_9_out ? bit_extender_3_out : 16'bz;  // Controlled_Buffer controlled_buffer_3
  assign bit_extender_3_out = {{4{1'b0}}, PC_q};  // Bit_Extender bit_extender_3
  and and_9 (and_9_out, ~P2_out, P1_out, ~P0_out);  // AND_Gate
  assign controlled_buffer_1_out = and_10_out ? MBR_q : 16'bz;  // Controlled_Buffer controlled_buffer_4
  and and_10 (and_10_out, ~P2_out, P1_out, P0_out);  // AND_Gate
  or or_7 (or_7_out, A1_2_out, A0_out);
  assign controlled_buffer_1_out = and_11_out ? AC_q : 16'bz;  // Controlled_Buffer controlled_buffer_5
  and and_11 (and_11_out, P2_out, ~P1_out, ~P0_out);  // AND_Gate
  assign controlled_buffer_1_out = and_7_out ? bit_extender_1_out : 16'bz;  // Controlled_Buffer controlled_buffer_6
  and and_12 (and_12_out, P2_out, ~P1_out, P0_out);  // AND_Gate
  assign controlled_buffer_1_out = and_13_out ? IR_q : 16'bz;  // Controlled_Buffer controlled_buffer_7
  and and_13 (and_13_out, P2_out, P1_out, P0_out);
  or or_8 (or_8_out, selector_1_error, xor_1_out, selector_1__7__halt);
  Selector selector_1 (
    .in_1(IR_q[15:12]), ._1__Load_X(selector_1__1__load_x), ._2__Store_X(selector_1__2__store_x),
    ._3__Add_X(selector_1__3__add_x), ._4__Subt_X(selector_1__4__subt_x), ._5__Input(selector_1__5__input),
    ._6__Output(selector_1__6__output), ._7__Halt(selector_1__7__halt),
    ._8__Skipcond__C(selector_1__8__skipcond__c), ._9__Jump_X(selector_1__9__jump_x), .ERROR(selector_1_error));  // open: _0__JnS_X, A__Clear, B__AddL_X, C__JumpL_X, D__StoreL, E__LoadL
  and L1 (L1_out, selector_1__1__load_x, T3_out);
  and L2 (L2_out, T4_out, selector_1__1__load_x);
  and L3 (L3_out, T5_out, selector_1__1__load_x);
  or P0 (P0_out, L1_out, L3_out, S1_out, S3_out, or_9_out, IN_out, JMP_out, in_1);
  and S1 (S1_out, selector_1__2__store_x, T3_out);
  or P1 (P1_out, T0_out, L1_out, L3_out, S1_out, S3_out, or_9_out, JMP_out, in_1);
  Hex_Digit_Display hex_digit_display_8 (.value(OutReg_q_2));  // open: dp
  Hex_Digit_Display hex_digit_display_9 (.value(OutReg_q_3));  // open: dp
  SkipCondCheck SkipCond_Check (
    .AC(AC_q), .DoesOpCodeCallForASkip(SKIP_out), .SkipCond(IR_q),
    .SkipConfirmed(SkipCond_Check_skipconfirmed));  // open: in_4
  and S2 (S2_out, selector_1__2__store_x, T4_out);
  and S3 (S3_out, selector_1__2__store_x, T5_out);
  Hex_Digit_Display hex_digit_display_10 (.value(OutReg_q[3:0]));  // open: dp
  Hex_Digit_Display hex_digit_display_11 (.value(OutReg_q[7:4]));  // open: dp
  and A1 (A1_out, selector_1__3__add_x, T3_out);
  and A2 (A2_out, selector_1__3__add_x, T4_out);
  or or_9 (or_9_out, A1_out, SU1_out);
  or or_10 (or_10_out, A2_out, SU2_out);
  or P2 (P2_out, L1_out, S1_out, S2_out, or_9_out, IN_out, OUT_out, JMP_out, in_1);
  and A3 (A3_out, selector_1__3__add_x, T5_out);
  and SU1 (SU1_out, selector_1__4__subt_x, T3_out);
  or P3 (P3_out, in_1, T0_out, T1_out, L1_out, L2_out, S1_out, S2_out, or_9_out, or_10_out, in_1);
  and SU2 (SU2_out, selector_1__4__subt_x, T4_out);
  and IN (IN_out, selector_1__5__input, T3_out);
  and SU3 (SU3_out, selector_1__4__subt_x, T5_out);
  or P4 (P4_out, T1_out, L2_out, S2_out, or_10_out, OUT_out, JMP_out, in_1, in_1);
  and OUT (OUT_out, selector_1__6__output, T3_out);
  or P5 (P5_out, T1_out, L3_out, A3_out, SU3_out, IN_out, OUT_out, in_1, in_1);
  and JMP (JMP_out, selector_1__9__jump_x, T3_out);
  and SKIP (SKIP_out, selector_1__8__skipcond__c, T3_out);
  or MR (MR_out, T1_out, L2_out, or_10_out, in_1, in_1, in_1, in_1, in_1);
  or MW (MW_out, S3_out, in_1, in_1, in_1, in_1, in_1, in_1, in_1);
  buf T0 (T0_out, Rung_Counter_t0);
  buf T1 (T1_out, Rung_Counter_t1);
  buf T2 (T2_out, Rung_Counter_t2);
  or IncrPC (IncrPC_out, T2_out, in_1, in_1, in_1, SkipCond_Check_skipconfirmed);
  Clock clock_1 (.out(clock_1_out));
  buf T3 (T3_out, Rung_Counter_t3);
  buf T5 (T5_out, Rung_Counter_t5);
  buf T4 (T4_out, Rung_Counter_t4);
  or A0 (A0_out, A3_out, in_1);
  and and_14 (and_14_out, clock_1_out, ~or_8_out);  // AND_Gate
  or A1_2 (A1_2_out, SU3_out, in_1);
  or LAlt (LAlt_out, L3_out, S2_out, in_1, in_1, in_1);
  or CR (CR_out, L3_out, S3_out, A3_out, IN_out, OUT_out, SKIP_out, JMP_out, in_1);
  RC Rung_Counter (
    .ClockIn(and_14_out), .ClockReset(CR_out), .T0(Rung_Counter_t0), .T1(Rung_Counter_t1),
    .T2(Rung_Counter_t2), .T3(Rung_Counter_t3), .T4(Rung_Counter_t4), .T5(Rung_Counter_t5));  // open: T6, T7

  // Notes on the sheet:
  //   P5 P4 P3
  //   P2 P1 P0
  //   OpCode
  //   MR
  //   MW
  //   IncrPC
  //   A0
  //   A1
  //   LAlt
  //   CR
  //   P0 P1 P2
  //   P3 P4 P5
endmodule

module Practice_Mem (
  input  in_1,
  input  in_2,
  input  in_3,
  input  [11:0] in_4,
  input  in_5,
  input  in_6,
  input  in_7
);

  wire clock_1_out, controlled_buffer_1_out;
  wire [7:0] counter_1_q, ram_1_data, random_1_out;
  wire [11:0] counter_2_q;

  Counter #(.ongoal("stay")) counter_1 (
    .Q(counter_1_q), .clk(controlled_buffer_1_out));  // open: load, D, count, carry, clr
  assign controlled_buffer_1_out = in_2 ? clock_1_out : 1'bz;  // Controlled_Buffer controlled_buffer_1
  Clock clock_1 (.out(clock_1_out));
  Random random_1 (.clk(clock_1_out), .out(random_1_out));  // open: next, clr
  RAM #(.bus("separate")) ram_1 (
    .addr(counter_1_q), .din(random_1_out), .data(ram_1_data), .clk(controlled_buffer_1_out), .ld(in_1));  // open: str, sel, clr
  Hex_Digit_Display hex_digit_display_1 (.value(ram_1_data[3:0]));  // open: dp
  Hex_Digit_Display hex_digit_display_2 (.value(ram_1_data[7:4]));  // open: dp
  Counter #(.width(12), .max('hfff)) counter_2 (
    .load(in_3), .D(in_4), .count(in_6), .Q(counter_2_q), .clk(in_7), .clr(in_5));  // open: carry
  Hex_Digit_Display hex_digit_display_3 (.value(counter_2_q[7:4]));  // open: dp
  Hex_Digit_Display hex_digit_display_4 (.value(counter_2_q[11:8]));  // open: dp
  Hex_Digit_Display hex_digit_display_5 (.value(counter_2_q[3:0]));  // open: dp
endmodule

module ALU (
  input  [15:0] MBR,
  input  [15:0] AC,
  input  A1,
  input  A0,
  output [15:0] Output
);

  wire [15:0] adder_1_out, subtractor_1_out;

  Adder #(.width(16)) adder_1 (.a(MBR), .b(AC), .out(adder_1_out));  // open: cin, cout
  Subtractor #(.width(16)) subtractor_1 (.a(AC), .b(MBR), .out(subtractor_1_out));  // open: bin, bout
  Multiplexer #(.select(2), .width(16)) multiplexer_1 (
    .in0({16{1'b1}}), .in1(adder_1_out), .in2(subtractor_1_out), .in3({16{1'b0}}), .out(Output),
    .sel({A1, A0}));  // open: en
endmodule

module Selector (
  input  [3:0] in_1,
  output _0__JnS_X,
  output _1__Load_X,
  output _2__Store_X,
  output _3__Add_X,
  output _4__Subt_X,
  output _5__Input,
  output _6__Output,
  output _7__Halt,
  output _8__Skipcond__C,
  output _9__Jump_X,
  output A__Clear,
  output B__AddL_X,
  output C__JumpL_X,
  output D__StoreL,
  output E__LoadL,
  output ERROR
);

  wire not_1_out, not_2_out, not_3_out, not_4_out;

  not not_1 (not_1_out, in_1[3]);
  not not_2 (not_2_out, in_1[2]);
  not not_3 (not_3_out, in_1[1]);
  not not_4 (not_4_out, in_1[0]);
  and _0_JnS_X (_0__JnS_X, not_4_out, not_3_out, not_2_out, not_1_out);
  and _1_Load_X (_1__Load_X, in_1[0], not_3_out, not_2_out, not_1_out);
  and _2_Store_X (_2__Store_X, not_4_out, in_1[1], not_2_out, not_1_out);
  and _3_Add_X (_3__Add_X, in_1[0], in_1[1], not_2_out, not_1_out);
  and _4_Subt_X (_4__Subt_X, not_4_out, not_3_out, in_1[2], not_1_out);
  and _5_Input (_5__Input, in_1[0], not_3_out, in_1[2], not_1_out);
  and _6_Output (_6__Output, not_4_out, in_1[1], in_1[2], not_1_out);
  and _7_Halt (_7__Halt, in_1[0], in_1[1], in_1[2], not_1_out);
  and _8_SkipCond_C (_8__Skipcond__C, not_4_out, not_3_out, not_2_out, in_1[3]);
  and _9_Jump_X (_9__Jump_X, in_1[0], not_3_out, not_2_out, in_1[3]);
  and A_Clear (A__Clear, not_4_out, in_1[1], not_2_out, in_1[3]);
  and B_AddL_X (B__AddL_X, in_1[0], in_1[1], not_2_out, in_1[3]);
  and C_JumpL_X (C__JumpL_X, not_4_out, not_3_out, in_1[2], in_1[3]);
  and u_D__StoreL (D__StoreL, in_1[0], not_3_out, in_1[2], in_1[3]);
  and E_LoadL (E__LoadL, not_4_out, in_1[1], in_1[2], in_1[3]);
  and F_DNC_ERROR (ERROR, in_1[0], in_1[1], in_1[2], in_1[3]);
endmodule

module RC (
  input  ClockIn,
  input  ClockReset,
  output T0,
  output T1,
  output T2,
  output T3,
  output T4,
  output T5,
  output T6,
  output T7
);

  wire nor_1_out;

  nor nor_1 (nor_1_out, T7, T6, T5, T4, T3, T2, T1, T0);
  D_Flip_Flop d_ff_1 (.clk(ClockIn), .D(nor_1_out), .Q(T0), .reset(ClockReset));  // open: Qn, preset, en
  D_Flip_Flop d_ff_2 (.clk(ClockIn), .D(T0), .Q(T1), .reset(ClockReset));  // open: Qn, preset, en
  D_Flip_Flop d_ff_3 (.clk(ClockIn), .D(T1), .Q(T2), .reset(ClockReset));  // open: Qn, preset, en
  D_Flip_Flop d_ff_4 (.clk(ClockIn), .D(T2), .Q(T3), .reset(ClockReset));  // open: Qn, preset, en
  D_Flip_Flop d_ff_5 (.clk(ClockIn), .D(T3), .Q(T4), .reset(ClockReset));  // open: Qn, preset, en
  D_Flip_Flop d_ff_6 (.clk(ClockIn), .D(T4), .Q(T5), .reset(ClockReset));  // open: Qn, preset, en
  D_Flip_Flop d_ff_7 (.clk(ClockIn), .D(T5), .Q(T6), .reset(ClockReset));  // open: Qn, preset, en
  D_Flip_Flop d_ff_8 (.clk(ClockIn), .D(T6), .Q(T7), .reset(ClockReset));  // open: Qn, preset, en
endmodule

module invertForSubt (
  input  invert,
  input  [15:0] datain,
  output [15:0] dataout
);

  xor xor_1 (dataout[0], datain[0], invert);
  xor xor_2 (dataout[1], datain[1], invert);
  xor xor_3 (dataout[2], datain[2], invert);
  xor xor_4 (dataout[3], datain[3], invert);
  xor xor_5 (dataout[12], datain[12], invert);
  xor xor_6 (dataout[13], datain[13], invert);
  xor xor_7 (dataout[14], datain[14], invert);
  xor xor_8 (dataout[15], datain[15], invert);
  xor xor_9 (dataout[4], datain[4], invert);
  xor xor_10 (dataout[5], datain[5], invert);
  xor xor_11 (dataout[6], datain[6], invert);
  xor xor_12 (dataout[7], datain[7], invert);
  xor xor_13 (dataout[8], datain[8], invert);
  xor xor_14 (dataout[9], datain[9], invert);
  xor xor_15 (dataout[10], datain[10], invert);
  xor xor_16 (dataout[11], datain[11], invert);
endmodule

module SkipCondCheck (
  input  [15:0] AC,
  input  DoesOpCodeCallForASkip,
  input  [15:0] SkipCond,
  input  in_4,
  output SkipConfirmed
);

  wire _0_out, _400_2_out, _400_out, _800_out, and_1_out, and_2_out, clock_1_out, ifAC_0_2_out, ifAC_0_3_out,
       ifAC_0_out, InRegA_q, or_1_out, undriven;

  Clock clock_1 (.out(clock_1_out));
  Register #(.width(1)) InRegA (.D(in_4), .Q(InRegA_q), .clk(clock_1_out), .clr(undriven));  // open: en
  and _0 (_0_out, ~SkipCond[0], ~SkipCond[1], ~SkipCond[2], ~SkipCond[3], ~SkipCond[4], ~SkipCond[5], ~SkipCond[6], ~SkipCond[7], ~SkipCond[8], ~SkipCond[9], ~SkipCond[10], ~SkipCond[11]);  // AND_Gate
  and _400 (_400_out, ~SkipCond[0], ~SkipCond[1], ~SkipCond[2], ~SkipCond[3], ~SkipCond[4], ~SkipCond[5], ~SkipCond[6], ~SkipCond[7], ~SkipCond[8], ~SkipCond[9], SkipCond[10], ~SkipCond[11]);  // AND_Gate
  and _800 (_800_out, ~SkipCond[0], ~SkipCond[1], ~SkipCond[2], ~SkipCond[3], ~SkipCond[4], ~SkipCond[5], ~SkipCond[6], ~SkipCond[7], ~SkipCond[8], ~SkipCond[9], ~SkipCond[10], SkipCond[11]);  // AND_Gate
  and ifAC_0 (ifAC_0_out, DoesOpCodeCallForASkip, _0_out);
  and ifAC_0_2 (ifAC_0_2_out, _400_out, DoesOpCodeCallForASkip);
  and ifAC_0_3 (ifAC_0_3_out, _800_out, DoesOpCodeCallForASkip);
  and and_1 (and_1_out, AC[15], ifAC_0_out);
  and _400_2 (_400_2_out, ~AC[0], ~AC[1], ~AC[2], ~AC[3], ~AC[4], ~AC[5], ~AC[6], ~AC[7], ~AC[8], ~AC[9], ~AC[10], ~AC[11], ~AC[12], ~AC[13], ~AC[14], ~AC[15], ifAC_0_2_out);  // AND_Gate
  or or_1 (or_1_out, AC[1], AC[2], AC[3], AC[4], AC[5], AC[6], AC[7], AC[0], AC[9], AC[10], AC[11], AC[12], AC[13], AC[14], AC[8]);
  and and_2 (and_2_out, ifAC_0_3_out, ~AC[15], or_1_out);  // AND_Gate
  or or_2 (SkipConfirmed, and_1_out, _400_2_out, and_2_out);
  // also tied to GND on the sheet: InRegA_q
endmodule
